# Fritzing sketch Controllo_LED_RGB (saved by Fritzing 0.8.0b)
breadboards: 1

parts:
  Arduino1 = Arduino
  LED1 = RGB LED (com. anode, rbg) [package="5 mm [THT]"]
  R5 = Resistor [tolerance=±5% resistance=220 package=THT]
  RE1 = Rotary Encoder [package=THT]
  RE2 = Rotary Encoder [package=THT]
  RE3 = Rotary Encoder [package=THT]

nets:
  N1: Arduino1.GND, RE1.EncoderPinA
  N2: Arduino1.D11, LED1.red_cathode
  N3: Arduino1.D10, LED1.blue_cathode
  N4: Arduino1.D9, LED1.green_cathode
  N5: Arduino1.+5V, R5.Pin_1, RE1.EncoderPinB
  N6: Arduino1.A0, RE1.EncoderPinC
  N7: Arduino1.A1, RE2.EncoderPinC
  N8: Arduino1.A2, RE3.EncoderPinC
  N9: LED1.common_anode, R5.Pin_0
  N10: RE2.EncoderPinA, RE3.EncoderPinA
  N11: RE2.EncoderPinB, RE3.EncoderPinB

// code stored in the sketch: color-Fader.ino
/*
  _____       .__  __         .__                
_/ ____\______|__|/  |________|__| ____    ____  
\   __\\_  __ \  \   __\___   /  |/    \  / ___\ 
 |  |   |  | \/  ||  |  /    /|  |   |  \/ /_/  >
 |__|   |__|  |__||__| /_____ \__|___|  /\___  / 
                             \/       \//_____/  
          __                 __                  __   .__  __   
  _______/  |______ ________/  |_  ___________  |  | _|__|/  |_ 
 /  ___/\   __\__  \\_  __ \   __\/ __ \_  __ \ |  |/ /  \   __\
 \___ \  |  |  / __ \|  | \/|  | \  ___/|  | \/ |    <|  ||  |  
/____  > |__| (____  /__|   |__|  \___  >__|    |__|_ \__||__|  
     \/            \/                 \/             \/         

Example      RGB LED Fader
Autor        Stefan Hermann
Date         16.06.2011

Description  This example lets you fade through the colors of a RGB LED.

*/

int LEDGreen=9;
int LEDBlue=10;
int LEDRed=11;


int sensorPin=0;
int val;

void setup(){
  Serial.begin(9600);
  pinMode(LEDRed,OUTPUT);
  pinMode(LEDGreen,OUTPUT);
  pinMode(LEDBlue,OUTPUT);  
}

void loop(){
  
  val=map(analogRead(sensorPin),0,1024,0,900);
  Serial.println(val);
  if (val<150) {
    analogWrite(LEDRed,0);
    analogWrite(LEDBlue,255); 
    analogWrite(LEDGreen,255);    
  } else if (val<300) {
    analogWrite(LEDRed,map(val,150,300,0,255));
    analogWrite(LEDBlue,map(val,150,300,255,0)); 
    analogWrite(LEDGreen,255);
  } else if (val<450) {
    analogWrite(LEDRed,255);
    analogWrite(LEDBlue,0); 
    analogWrite(LEDGreen,255);  
  } else if (val<600) {
    analogWrite(LEDRed,255);
    analogWrite(LEDBlue,map(val,450,600,0,255)); 
    analogWrite(LEDGreen,map(val,450,600,255,0));
  } else if (val<750) {
    analogWrite(LEDRed,255);
    analogWrite(LEDBlue,255); 
    analogWrite(LEDGreen,0);  
  } else if (val<900) {
    analogWrite(LEDRed,map(val,750,900,255,0));
    analogWrite(LEDBlue,255); 
    analogWrite(LEDGreen,map(val,750,900,0,255));
  }
  delay(10);
}
