# Fritzing sketch Controllo_LED_con_interfaccia_LCD (saved by Fritzing 0.8.0b)
breadboards: 1

parts:
  LCD1 = LCD screen
  R2 = Resistor [tolerance=±5% resistance=220 package=THT]
  Arduino1 = Arduino Uno (Rev3)
  RE1 = Rotary Encoder [package=THT]
  RE2 = Rotary Encoder [package=THT]
  LED1 = LED - 3mm [color="Red (633nm)" package="3 mm [THT]"]

nets:
  VSS: LCD1.VSS, LCD1.R/W, LCD1.LED-, Arduino1.GND, RE1.EncoderPinB, RE2.EncoderPinB, LED1.cathode
  VDD: LCD1.VDD, R2.Pin_1, Arduino1.5V, RE1.EncoderPinA, RE2.EncoderPinA
  N1: LCD1.V0, RE1.EncoderPinC
  N2: LCD1.RS, Arduino1.D12/MISO
  N3: LCD1.E, Arduino1.D11_PWM/MOSI
  N4: LCD1.DB4, Arduino1.D5_PWM
  N5: LCD1.DB5, Arduino1.D4
  N6: LCD1.DB6, Arduino1.D3_PWM
  N7: LCD1.DB7, Arduino1.D2
  N8: LCD1.LED+, R2.Pin_0
  N9: Arduino1.A0, RE2.EncoderPinC
  N10: Arduino1.D10_PWM/SS, LED1.anode
