# Fritzing sketch Controllo_PWM_LED_con_potenziometri (saved by Fritzing 0.8.0b)
breadboards: 1

parts:
  LED2 = LED - 5mm [color="Red (635nm)" package="5 mm [THT]"]
  Arduino2 = Arduino Uno (Rev3)
  R1 = Rotary Potentiometer (Small) [maximum_resistance=100kΩ]

nets (from the breadboard view):
  N1: LED2.cathode, Arduino2.GND, R1.leg1
  N2: LED2.anode, Arduino2.ICSP_MOSI, Arduino2.D11_PWM/MOSI
  N3: Arduino2.A0, R1.wiper
  N4: Arduino2.ICSP_SCK, Arduino2.D13/SCK
  N5: Arduino2.5V, R1.leg2
