# Fritzing sketch Controllo_bidirezionale_di_due_motori_DC (saved by Fritzing 0.8.0b)
breadboards: 1

parts:
  IC1 = H-Bridge [package=THT]
  R2 = Resistor [resistance=1k tolerance=±5% package=THT]
  S2 = Pushbutton [package=THT]
  M1 = DC Motor
  Arduino2 = Arduino
  M2 = DC Motor
  R3 = Resistor [resistance=1k tolerance=±5% package=THT]
  S3 = Pushbutton [package=THT]
  R4 = Rotary Potentiometer (Small) [maximum_resistance=100kΩ]
  R5 = Rotary Potentiometer (Small) [maximum_resistance=100kΩ]

nets:
  N1: IC1.1_2EN, Arduino2.D4
  N2: IC1.1A, Arduino2.D10
  N3: IC1.1Y, M1.pin_2
  GND1: IC1.GND1, IC1.GND2, IC1.GND3, IC1.GND4, R2.Pin_0, Arduino2.GND, R3.Pin_0, R4.leg2, R5.leg2
  N4: IC1.2Y, M1.pin_1
  N5: IC1.2A, Arduino2.D9
  N6: IC1.VCC2, Arduino2.3V3
  N7: IC1.3_4EN, Arduino2.D7
  N8: IC1.3A, Arduino2.D6
  N9: IC1.3Y, M2.pin_2
  N10: IC1.4Y, M2.pin_1
  N11: IC1.4A, Arduino2.D11
  N12: IC1.VCC1, S2.leg0, Arduino2.+5V, S3.leg0, R4.leg1, R5.leg1
  N13: R2.Pin_1, S2.leg1, Arduino2.D2
  N14: Arduino2.D3, R3.Pin_1, S3.leg1
  N15: Arduino2.A0, R4.wiper
  N16: Arduino2.A1, R5.wiper
