# Fritzing sketch Controllo_di_servomotori_con_potenziometri_e_sensori (saved by Fritzing 0.8.0b)
breadboards: 1

parts:
  J1 = Basic Servo
  Arduino2 = Arduino Uno (Rev3)
  R6 = Photocell (LDR) [package=THT]
  R7 = Resistor [tolerance=±5% resistance=10k package=THT]
  J2 = Basic Servo
  RE1 = Rotary Encoder [package=THT]
  BATT1 = LiPoly Battery (1300mAh)

nets:
  GND: J1.gnd, Arduino2.GND, R7.Pin_1, J2.gnd, RE1.EncoderPinB, BATT1.negative
  VCC: J1.vcc, J2.vcc, BATT1.positive
  N1: J1.pulse, Arduino2.D3_PWM
  N2: Arduino2.A0, R6.pin_1, R7.Pin_0
  N3: Arduino2.A1, RE1.EncoderPinC
  N4: Arduino2.D2, J2.pulse
  N5: Arduino2.5V, R6.pin_0, RE1.EncoderPinA

custom parts:
  LiPoly Battery (1300mAh): Lithium Ion Polymer Battery (1300mAh)
