# Fritzing sketch Controllo_due_motori_DC_con_transistor (saved by Fritzing 0.8.0b)
breadboards: 1

parts:
  Arduino2 = Arduino Uno (Rev3)
  Q1 = NPN-Transistor [part_number=BC547 package="TO92 [THT]"]
  VCC1 = Battery
  M1 = DC Motor
  M2 = DC Motor
  Q2 = NPN-Transistor [part_number=BC547 package="TO92 [THT]"]
  D2 = Rectifier Diode [part_number=1N4001 package="300 mil [THT]"]
  RE1 = Rotary Encoder [package=THT]
  RE2 = Rotary Encoder [package=THT]
  D1 = Rectifier Diode [part_number=1N4001 package="300 mil [THT]"]

nets:
  N1: Arduino2.A0, RE2.EncoderPinC
  N2: Arduino2.A1, RE1.EncoderPinC
  N3: Arduino2.ICSP_MOSI, Arduino2.D11_PWM/MOSI, Q2.B
  N4: Arduino2.D6_PWM, Q1.B
  N5: Arduino2.5V, RE1.EncoderPinA, RE2.EncoderPinA
  N6: Q1.E, M1.pin_2, D1.cathode
  N7: Q1.C, VCC1.-, Q2.C, D2.anode, RE1.EncoderPinB, RE2.EncoderPinB, D1.anode
  N8: VCC1.+, M1.pin_1, M2.pin_1
  N9: M2.pin_2, Q2.E, D2.cathode
