# Fritzing sketch Controllo_relay_con_sensore (saved by Fritzing 0.8.0b)
breadboards: 1

parts:
  Arduino1 = Arduino Uno (Rev3)
  Power_plug2 = Power plug  # not connected
  R4 = Resistor [resistance=1k tolerance=±5% package=THT]
  K2 = Relay [part_number=FRS1B-S package=THT]
  Q3 = NPN-Transistor [package="TO92 [THT]"]
  R5 = Resistor [tolerance=±5% resistance=10k package=THT]
  D1 = Rectifier Diode [part_number=1N4001 package="300 mil [THT]"]  # not connected

nets:
  N1: Arduino1.GND, Q3.C, R5.Pin_1
  N2: Arduino1.D13/SCK, R4.Pin_1
  N3: Arduino1.5V, K2.COIL2
  N4: R4.Pin_0, Q3.B, R5.Pin_0
  N5: K2.COIL1, Q3.E
  N6: K2.C1, K2.C2

notes:
  Carico 220 V
