# Fritzing sketch Display_7_segmenti_conteggio_0_9 (saved by Fritzing 0.8.0b)
breadboards: 1

parts:
  Arduino2 = Arduino
  7_Segment2 = 7 Segment Display

nets:
  N1: Arduino2.GND, 7_Segment2.common_cathode
  N2: Arduino2.D13, 7_Segment2.Segment_DP
  N3: Arduino2.D12, 7_Segment2.Segment_G
  N4: Arduino2.D11, 7_Segment2.Segment_F
  N5: Arduino2.D10, 7_Segment2.Segment_E
  N6: Arduino2.D9, 7_Segment2.Segment_D
  N7: Arduino2.D8, 7_Segment2.Segment_C
  N8: Arduino2.D7, 7_Segment2.Segment_B
  N9: Arduino2.D6, 7_Segment2.Segment_A
