# Fritzing sketch Generatore_di_funzioni (saved by Fritzing 0.8.0b)
breadboards: 1

parts:
  LCD1 = LCD screen
  Arduino1 = Arduino Uno (Rev3)
  RE1 = Rotary Encoder [package=THT]
  TRRS1 = Audio Jack (TRRS) 3.5mm [part_number="LUMBERG JEITA RC-5325A" package="RC-5325A [SMD]"]
  S3 = Pushbutton [package="[THT]"]
  RE2 = Rotary Encoder [package=THT]
  R1 = Resistor [tolerance=±5% resistance=10k package=THT]

nets:
  VSS: LCD1.VSS, LCD1.R/W, LCD1.LED-, Arduino1.GND, RE1.EncoderPinB, TRRS1.TIP, RE2.EncoderPinB, R1.Pin_1
  VDD: LCD1.VDD, LCD1.LED+, Arduino1.5V, RE1.EncoderPinA, S3.Pin_3, S3.Pin_4, RE2.EncoderPinA
  N1: LCD1.V0, RE1.EncoderPinC
  N2: LCD1.RS, Arduino1.D12/MISO
  N3: LCD1.E, Arduino1.D11_PWM/MOSI
  N4: LCD1.DB4, Arduino1.D6_PWM
  N5: LCD1.DB5, Arduino1.D5_PWM
  N6: LCD1.DB6, Arduino1.D4
  N7: LCD1.DB7, Arduino1.D2
  N8: Arduino1.A5/SCL, RE2.EncoderPinC
  N9: Arduino1.ICSP_SCK, Arduino1.D13/SCK, S3.Pin_1, S3.Pin_2, R1.Pin_0
  N10: Arduino1.D3_PWM, TRRS1.SLEEVE
