# Fritzing sketch Interfaccia_sensore_display_7_segmenti (saved by Fritzing 0.8.0b)
breadboards: 1

parts:
  Arduino2 = Arduino
  7_Segment2 = 7 Segment Display
  R2 = Photocell (LDR) [package=THT]
  R3 = Resistor [tolerance=±5% resistance=10k package=THT]

nets:
  N1: Arduino2.GND, 7_Segment2.common_cathode, R3.Pin_1
  N2: Arduino2.D13, 7_Segment2.Segment_DP
  N3: Arduino2.D12, 7_Segment2.Segment_G
  N4: Arduino2.D11, 7_Segment2.Segment_F
  N5: Arduino2.D10, 7_Segment2.Segment_E
  N6: Arduino2.D9, 7_Segment2.Segment_D
  N7: Arduino2.D8, 7_Segment2.Segment_C
  N8: Arduino2.D7, 7_Segment2.Segment_B
  N9: Arduino2.D6, 7_Segment2.Segment_A
  N10: Arduino2.+5V, R2.pin_0
  N11: Arduino2.A0, R2.pin_1, R3.Pin_0
