# Fritzing sketch Orologio_controllato_da_Web (saved by Fritzing 0.8.0b)
breadboards: 1

parts:
  LCD1 = LCD screen
  R2 = Resistor [tolerance=±5% resistance=220 package=THT]
  R13 = Trimmer Potentiometer [maximum_resistance=10kΩ package=THT]
  Componente2 = Arduino Ethernet Shield (Rev3)

nets:
  VSS: LCD1.VSS, LCD1.R/W, LCD1.LED-, R13.leg2, Componente2.GND
  VDD: LCD1.VDD, R2.Pin_1, R13.leg1, Componente2.5V
  N1: LCD1.V0, R13.wiper
  N2: LCD1.RS, Componente2.D7
  N3: LCD1.E, Componente2.PWM_D6
  N4: LCD1.DB4, Componente2.PWM_D5
  N5: LCD1.DB5, Componente2.SDCS
  N6: LCD1.DB6, Componente2.PWM_D3
  N7: LCD1.DB7, Componente2.D2
  N8: LCD1.LED+, R2.Pin_0
