# Fritzing sketch Oscilloscopio_con_display_grafico (saved by Fritzing 0.8.0b)
breadboards: 1

parts:
  GLCD_128x1 = 128 x 64 Graphic LCD
  Arduino1 = Arduino
  R1 = Rotary Potentiometer (Small) [maximum_resistance=10kΩ]
  R2 = Resistor [tolerance=±5% resistance=220 package=THT]  # not connected

nets (from the pcb view):
  N1: GLCD_128x1.1_Vss, GLCD_128x1.20_K(-), Arduino1.GND, R1.leg2
  N2: GLCD_128x1.3_Vo, R1.leg1
  N3: GLCD_128x1.4_D/I, Arduino1.RST
  N4: GLCD_128x1.5_R/W, Arduino1.A1
  N5: GLCD_128x1.6_Enable, Arduino1.A0
  N6: GLCD_128x1.7_DB0, Arduino1.D7
  N7: GLCD_128x1.8_DB1, Arduino1.D6
  N8: GLCD_128x1.9_BD2, Arduino1.D5
  N9: GLCD_128x1.10_DB3, Arduino1.D4
  N10: GLCD_128x1.11_DB4, Arduino1.D11
  N11: GLCD_128x1.12_DB5, Arduino1.D10
  N12: GLCD_128x1.13_DB6, Arduino1.D9
  N13: GLCD_128x1.14_DB7, Arduino1.D8
  N14: GLCD_128x1.15_CS1, Arduino1.A4
  N15: GLCD_128x1.16_CS2, Arduino1.A2
  N16: GLCD_128x1.17_RST, Arduino1.A3
  N17: GLCD_128x1.18_Vout, R1.wiper
  N18: GLCD_128x1.19_A(+), Arduino1.+5V
