# Fritzing sketch Rover_con_controllo_Wi_Fi (saved by Fritzing 0.8.0b)
breadboards: 1

parts:
  Arduino1 = Arduino
  M1 = DC Motor
  M2 = DC Motor
  IC1 = L293D [package=THT]
  Componente5 = Bluetooth Module Breakout - Roving Networks (RN-41)
  RE2 = Rotary Encoder [package=THT]
  LCD2 = LCD screen
  R3 = Resistor [tolerance=±5% resistance=220 package=THT]

nets:
  N1: Arduino1.D13, LCD2.RS
  N2: Arduino1.D12, IC1.In_2
  N3: Arduino1.D11, IC1.In_4
  N4: Arduino1.D10, IC1.In_1
  N5: Arduino1.D9, LCD2.E
  N6: Arduino1.D8, IC1.In_3
  N7: Arduino1.D7, IC1.Enable_2
  N8: Arduino1.D6, LCD2.DB3
  N9: Arduino1.D5, LCD2.DB4
  N10: Arduino1.D4, IC1.Enable_1
  N11: Arduino1.D3, LCD2.DB5
  N12: Arduino1.D2, LCD2.DB6
  N13: Arduino1.D1TX, Componente5.10
  N14: Arduino1.D0RX, Componente5.PIO11
  +5V: Arduino1.+5V, IC1.+V, Componente5.VCC, RE2.EncoderPinA, LCD2.VDD
  GND: Arduino1.GND, Componente5.GND, RE2.EncoderPinB, LCD2.VSS, LCD2.R/W, LCD2.LED+
  N15: M1.pin_1, IC1.Out_2_(_Controlled_by_Enable_1_)
  N16: M1.pin_2, IC1.Out_1_(_Controlled_by_Enable_1_)
  N17: M2.pin_1, IC1.Out_4_(_Controlled_by_Enable_2_)
  N18: M2.pin_2, IC1.Out_3_(_Controlled_by_Enable_2_)
  N19: RE2.EncoderPinC, LCD2.V0
  N20: LCD2.DB7, R3.Pin_0
