# Fritzing sketch Card SD con interfaccia LCD (saved by Fritzing 0.8.3b)
circuit board: 6.88561cm x 5.36311cm
breadboards: 1

parts:
  LCD1 = LCD screen
  R2 = Resistor [tolerance=±5% resistance=220 package=THT]
  Arduino1 = Arduino Uno (Rev3)
  R7 = Resistor [tolerance=±5% resistance=3.3k package=THT]
  R8 = Resistor [tolerance=±5% resistance=3.3k package=THT]
  R9 = Resistor [tolerance=±5% resistance=3.3k package=THT]
  R10 = Resistor [tolerance=±5% resistance=1.8k package=THT]
  R11 = Resistor [tolerance=±5% resistance=1.8k package=THT]
  R12 = Resistor [tolerance=±5% resistance=1.8k package=THT]
  J2 = female pin header, 7 pins [form="♀ (female)"]
  R13 = Trimmer Potentiometer [maximum_resistance=10kΩ package=THT]

nets:
  VSS: LCD1.VSS, LCD1.R/W, LCD1.LED-, Arduino1.GND, J2.pin3, R13.leg2
  VDD: LCD1.VDD, R2.Pin_1, Arduino1.5V, R13.leg1
  N1: LCD1.V0, R13.wiper
  N2: LCD1.RS, Arduino1.D7
  N3: LCD1.E, Arduino1.D6_PWM
  N4: LCD1.DB4, Arduino1.D5_PWM
  N5: LCD1.DB5, Arduino1.D4
  N6: LCD1.DB6, Arduino1.D3_PWM
  N7: LCD1.DB7, Arduino1.D2
  N8: LCD1.LED+, R2.Pin_0
  N9: Arduino1.ICSP_MISO, Arduino1.D12/MISO, J2.pin7
  N10: Arduino1.ICSP_SCK, Arduino1.D13/SCK, R10.Pin_0
  N11: Arduino1.ICSP_MOSI, Arduino1.D11_PWM/MOSI, R11.Pin_0
  N12: Arduino1.D10_PWM/SS, R12.Pin_0
  N13: Arduino1.3V3, J2.pin4
  N14: R7.Pin_0, R8.Pin_0, R9.Pin_0
  N15: R7.Pin_1, R11.Pin_1, J2.pin2
  N16: R8.Pin_1, R12.Pin_1, J2.pin1
  N17: R9.Pin_1, R10.Pin_1, J2.pin5

notes:
  1 2 3 4 5 6 7
  SD CARD
