# Fritzing sketch Collegare una card SD ad Arduino (saved by Fritzing 0.8.0b)
breadboards: 1

parts:
  R1 = Resistor [tolerance=±5% resistance=3.3k package=THT]
  R2 = Resistor [tolerance=±5% resistance=3.3k package=THT]
  R3 = Resistor [tolerance=±5% resistance=3.3k package=THT]
  R4 = Resistor [tolerance=±5% resistance=1.8k package=THT]
  R5 = Resistor [tolerance=±5% resistance=1.8k package=THT]
  R6 = Resistor [tolerance=±5% resistance=1.8k package=THT]
  Componente1 = Arduino Uno (Rev3)
  J1 = female pin header, 7 pins [form="♀ (female)"]

nets:
  N1: R1.Pin_0, R2.Pin_0, R3.Pin_0, Componente1.GND, J1.pin3, J1.pin6
  N2: R1.Pin_1, R5.Pin_1, J1.pin5
  N3: R2.Pin_1, R6.Pin_1, J1.pin2
  N4: R3.Pin_1, R4.Pin_1, J1.pin1
  N5: R4.Pin_0, Componente1.D10_PWM/SS
  N6: R5.Pin_0, Componente1.ICSP_SCK, Componente1.D13/SCK
  N7: R6.Pin_0, Componente1.D11_PWM/MOSI
  N8: Componente1.D12/MISO, J1.pin7
  N9: Componente1.3V3, J1.pin4

notes:
  1 2 3 4 5 6 7
  SD CARD
