# Fritzing sketch Termometro_con_visualizzazione_su_display (saved by Fritzing 0.8.3b)
circuit board: 6.88561cm x 5.36311cm
breadboards: 1

parts:
  LCD1 = LCD screen
  R2 = Resistor [tolerance=±5% resistance=220 package=THT]
  Arduino1 = Arduino Uno (Rev3)
  RE1 = Rotary Encoder [package=THT]
  U4 = LM35 [package="TO220 [THT]"]  # not connected

nets:
  VSS: LCD1.VSS, LCD1.R/W, LCD1.LED-, Arduino1.GND, RE1.EncoderPinB
  VDD: LCD1.VDD, R2.Pin_1, Arduino1.5V, RE1.EncoderPinA
  N1: LCD1.V0, RE1.EncoderPinC
  N2: LCD1.RS, Arduino1.D12/MISO
  N3: LCD1.E, Arduino1.D11_PWM/MOSI
  N4: LCD1.DB4, Arduino1.D5_PWM
  N5: LCD1.DB5, Arduino1.D4
  N6: LCD1.DB6, Arduino1.D3_PWM
  N7: LCD1.DB7, Arduino1.D2
  N8: LCD1.LED+, R2.Pin_0

custom parts:
  LM35: Temperature sensor
