# Fritzing sketch Uso_del_sensore_di_tilt (saved by Fritzing 0.8.0b)
breadboards: 1

parts:
  Arduino1 = Arduino Uno (Rev3)
  Switch = Tilt Switch [package=THT]
  R1 = Resistor [tolerance=±5% resistance=100k package=THT]

nets:
  N1: Arduino1.GND, R1.Pin_0
  N2: Arduino1.D8, Switch.Pin_1, R1.Pin_1
  N3: Arduino1.5V, Switch.Pin_2
