# Fritzing sketch VU_meter_a_LED (saved by Fritzing 0.8.0b)
breadboards: 1

parts:
  LED2 = LED - 5mm [color="Green (570nm)" package="5 mm [THT]"]
  Arduino2 = Arduino Uno (Rev3)
  LED3 = LED - 5mm [color="Green (570nm)" package="5 mm [THT]"]
  LED4 = LED - 5mm [color="Green (570nm)" package="5 mm [THT]"]
  LED5 = LED - 5mm [color="Yellow (595nm)" package="5 mm [THT]"]
  LED6 = LED - 5mm [color="Yellow (595nm)" package="5 mm [THT]"]
  LED7 = LED - 5mm [color="Red (635nm)" package="5 mm [THT]"]
  LED8 = LED - 5mm [color="Orange (620nm)" package="5 mm [THT]"]
  LED9 = LED - 5mm [color="Yellow (595nm)" package="5 mm [THT]"]
  LED10 = LED - 5mm [color="Red (635nm)" package="5 mm [THT]"]
  LED11 = LED - 5mm [color="Red (635nm)" package="5 mm [THT]"]
  R1 = Resistor [tolerance=±5% resistance=220 package=THT]
  R2 = Resistor [tolerance=±5% resistance=220 package=THT]
  R3 = Resistor [tolerance=±5% resistance=220 package=THT]
  R4 = Resistor [tolerance=±5% resistance=220 package=THT]
  R5 = Resistor [tolerance=±5% resistance=220 package=THT]
  R6 = Resistor [tolerance=±5% resistance=220 package=THT]
  R7 = Resistor [tolerance=±5% resistance=220 package=THT]
  R8 = Resistor [tolerance=±5% resistance=220 package=THT]
  R9 = Resistor [tolerance=±5% resistance=220 package=THT]
  R10 = Resistor [tolerance=±5% resistance=220 package=THT]
  TRRS1 = Audio Jack (TRRS) 3.5mm [part_number="LUMBERG JEITA RC-5325A" package="RC-5325A [SMD]"]

nets:
  N1: LED2.cathode, Arduino2.GND, LED3.cathode, LED4.cathode, LED5.cathode, LED6.cathode, LED7.cathode, LED8.cathode, LED9.cathode, LED10.cathode, LED11.cathode, TRRS1.TIP
  N2: LED2.anode, R1.Pin_1
  N3: Arduino2.A0, TRRS1.SLEEVE
  N4: Arduino2.ICSP_MOSI, Arduino2.D11_PWM/MOSI, R10.Pin_0
  N5: Arduino2.D8, R7.Pin_0
  N6: Arduino2.D9_PWM, R8.Pin_0
  N7: Arduino2.D10_PWM/SS, R9.Pin_0
  N8: Arduino2.D2, R1.Pin_0
  N9: Arduino2.D3_PWM, R2.Pin_0
  N10: Arduino2.D4, R3.Pin_0
  N11: Arduino2.D5_PWM, R4.Pin_0
  N12: Arduino2.D6_PWM, R5.Pin_0
  N13: Arduino2.D7, R6.Pin_0
  N14: LED3.anode, R2.Pin_1
  N15: LED4.anode, R3.Pin_1
  N16: LED5.anode, R4.Pin_1
  N17: LED6.anode, R5.Pin_1
  N18: LED7.anode, R8.Pin_1
  N19: LED8.anode, R7.Pin_1
  N20: LED9.anode, R6.Pin_1
  N21: LED10.anode, R10.Pin_1
  N22: LED11.anode, R9.Pin_1
