# Fritzing sketch VU_meter_con_10_LED (saved by Fritzing 0.8.0b)
breadboards: 1

parts:
  Contrast = Rotary Potentiometer (Small) [maximum_resistance=100kΩ]
  LCD = LCD screen
  LCD_Shield = Arduino
  TRRS1 = Audio Jack (TRRS) 3.5mm [part_number="LUMBERG JEITA RC-5325A" package="RC-5325A [SMD]"]

nets (from the breadboard view):
  VSS: Contrast.leg1, LCD.VSS, LCD.R/W, LCD.LED-, LCD_Shield.GND, LCD_Shield.D11, TRRS1.TIP
  N1: Contrast.wiper, LCD.V0
  VDD: Contrast.leg2, LCD.VDD, LCD.LED+, LCD_Shield.+5V
  N2: LCD.RS, LCD_Shield.D12
  N3: LCD.DB4, LCD_Shield.D6
  N4: LCD.DB5, LCD_Shield.D5
  N5: LCD.DB6, LCD_Shield.D4
  N6: LCD.DB7, LCD_Shield.D2
  N7: LCD_Shield.A0, TRRS1.SLEEVE
  N8: LCD_Shield.A1, TRRS1.RING2

// code stored in the sketch: LiquidCrystalDisplay.ino
/*
  LiquidCrystal Library - Hello World
 
 Demonstrates the use a 16x2 LCD display.  The LiquidCrystal
 library works with all LCD displays that are compatible with the 
 Hitachi HD44780 driver. There are many of them out there, and you
 can usually tell them by the 16-pin interface.
 
 This sketch prints "Hello World!" to the LCD
 and shows the time.
 
  The circuit:
 * LCD RS pin to digital pin 12
 * LCD Enable pin to digital pin 11
 * LCD D4 pin to digital pin 5
 * LCD D5 pin to digital pin 4
 * LCD D6 pin to digital pin 3
 * LCD D7 pin to digital pin 2
 * LCD R/W pin to ground
 * 10K resistor:
 * ends to +5V and ground
 * wiper to LCD VO pin (pin 3)
 
 Library originally added 18 Apr 2008
 by David A. Mellis
 library modified 5 Jul 2009
 by Limor Fried (http://www.ladyada.net)
 example added 9 Jul 2009
 by Tom Igoe
 modified 22 Nov 2010
 by Tom Igoe
 
 This example code is in the public domain.

 http://www.arduino.cc/en/Tutorial/LiquidCrystal
 */

// include the library code:
#include <LiquidCrystal.h>

// initialize the library with the numbers of the interface pins
LiquidCrystal lcd(12, 11, 5, 4, 3, 2);

void setup() {
  // set up the LCD's number of columns and rows: 
  lcd.begin(16, 2);
  // Print a message to the LCD.
  lcd.print("hello, world!");
}

void loop() {
  // set the cursor to column 0, line 1
  // (note: line 1 is the second row, since counting begins with 0):
  lcd.setCursor(0, 1);
  // print the number of seconds since reset:
  lcd.print(millis()/1000);
}
